# Fritzing sketch MacroKeyTouchSensor (saved by Fritzing 0.9.3b)
breadboards: 1

parts:
  Part1 = MPR121 Breakout
  Raspberry_Pi_1 = Raspberry Pi 3 [part_number=RPI-3-V1.2]

nets:
  N1: Part1.SCL, Raspberry_Pi_1.GPIO3
  N2: Part1.SDA, Raspberry_Pi_1.GPIO2
  3.3V: Part1.3.3V, Raspberry_Pi_1.3v3
  GND: Part1.GND, Raspberry_Pi_1.GND
