# Fritzing sketch MacroKeyTouchSensor2 (saved by Fritzing 0.9.3b)
circuit board: 8.46667cm x 5.64444cm
breadboards: 1

parts:
  J1 = female pin header, 1 pin [form="♀ (female)"]  # not connected
  J2 = female pin header, 1 pin [form="♀ (female)"]
  Raspberry_Pi_1 = Raspberry Pi 3 [part_number=RPI-3-V1.2]
  J3 = female pin header, 13 pins [form="♀ (female)"]
  J4 = female pin header, 1 pin [form="♀ (female)"]
  J5 = female pin header, 1 pin [form="♀ (female)"]
  J6 = female pin header, 1 pin [form="♀ (female)"]  # not connected
  J7 = female pin header, 1 pin [form="♀ (female)"]
  J8 = female pin header, 1 pin [form="♀ (female)"]  # not connected
  J9 = female pin header, 1 pin [form="♀ (female)"]
  J10 = female pin header, 1 pin [form="♀ (female)"]
  J11 = female pin header, 1 pin [form="♀ (female)"]
  J12 = female pin header, 1 pin [form="♀ (female)"]
  J13 = female pin header, 1 pin [form="♀ (female)"]
  J14 = female pin header, 1 pin [form="♀ (female)"]
  J15 = female pin header, 1 pin [form="♀ (female)"]
  J16 = female pin header, 1 pin [form="♀ (female)"]
  J17 = female pin header, 1 pin [form="♀ (female)"]
  J18 = female pin header, 1 pin [form="♀ (female)"]
  J19 = female pin header, 1 pin [form="♀ (female)"]
  J20 = female pin header, 1 pin [form="♀ (female)"]
  J21 = female pin header, 1 pin [form="♀ (female)"]

nets:
  N1: J2.pin1, J3.pin13
  N2: Raspberry_Pi_1.3v3, J9.pin1
  N3: Raspberry_Pi_1.GPIO2, J5.pin1
  N4: Raspberry_Pi_1.GPIO3, J4.pin1
  N5: Raspberry_Pi_1.GND, J7.pin1
  N6: J3.pin1, J21.pin1
  N7: J3.pin2, J20.pin1
  N8: J3.pin3, J19.pin1
  N9: J3.pin4, J18.pin1
  N10: J3.pin5, J17.pin1
  N11: J3.pin6, J16.pin1
  N12: J3.pin7, J15.pin1
  N13: J3.pin8, J14.pin1
  N14: J3.pin9, J12.pin1
  N15: J3.pin10, J11.pin1
  N16: J3.pin11, J13.pin1
  N17: J3.pin12, J10.pin1

notes:
  Vin
  3Vo
  GND
  ADDR
  SDA
  SCL
  IRQ
  0
  11
  10
  9
  8
  5
  4
  7
  6
  3
  2
  1
  Jonas Gamao
  N01198081
